# Fritzing sketch sketch (saved by Fritzing 0.9.3b)
breadboards: 1

parts:
  U1 = NodeMCU V1.0
  PIR1 = PIR sensor
  LED1 = smd LED [color="Red (633nm)" package="0805 [SMD]"]
  R2 = Resistor [tolerance=±5% resistance=220 package=THT]
  LED2 = LED - 5mm [color="Blue (430nm)" package="5 mm [THT]"]
  R3 = Resistor [tolerance=±5% resistance=220 package=THT]
  DHT1 = DHT11 Humitidy and Temperature Sensor
  R4 = Resistor [tolerance=±5% resistance=220 package=THT]
  U2 = GAS_SENSOR [package=mq-3]

nets:
  N1: U1.D2, DHT1.DATA, R4.Pin_0
  N2: U1.D3, R2.Pin_0
  N3: U1.D4, R3.Pin_0
  3V3: U1.3V3, DHT1.VDD, R4.Pin_1
  GND: U1.GND, PIR1.GND, LED1.cathode, LED2.cathode, DHT1.GND, U2.H1
  N4: U1.D5, PIR1.SIG
  VIN: U1.Vin, PIR1.VDD
  N5: U1.A0, U2.H2
  N6: LED1.anode, R3.Pin_1
  N7: R2.Pin_1, LED2.anode

custom parts:
  NodeMCU V1.0: ESP8266 based NodeMCU
  DHT11 Humitidy and Temperature Sensor: DHT11 Humidity and Temperature Sensor
