# Fritzing sketch v20 (saved by Fritzing 0.9.3b)
perfboards: 1

parts:
  U3 = NodeMCU V1.0
  Part2 = Bluetooth HM-10
  J5 = female pin header, 3 pins [form="♀ (female)"]
  J6 = female pin header, 4 pins [form="♀ (female)"]
  J7 = female pin header, 3 pins [form="♀ (female)"]
  J8 = female pin header, 4 pins [form="♀ (female)"]
  LED3 = smd LED [color="Blue (430nm)" package="1206 [SMD]"]
  LED4 = smd LED [color="Red (633nm)" package="1206 [SMD]"]
  R3 = Resistor [tolerance=±5% resistance=220 package=THT]
  R4 = Resistor [tolerance=±5% resistance=220 package=THT]
  DHT2 = DHT11 Humitidy and Temperature Sensor
  PIR2 = PIR sensor
  U4 = GAS_SENSOR [package=mq-3]  # not connected

nets:
  N1: U3.D0, J7.pin2, PIR2.SIG
  N2: U3.D1, R3.Pin_0
  N3: U3.D2, R4.Pin_0
  N4: U3.3V3, J8.pin1
  GND: U3.GND, J7.pin1, J8.pin2, PIR2.GND
  VIN: U3.Vin, J7.pin3, PIR2.VDD
  N5: U3.A0, J8.pin4
  N6: Part2.RXD, J6.pin4
  N7: Part2.TXD, J6.pin3
  N8: Part2.GND, J6.pin2
  N9: Part2.VCC, J6.pin1
  N10: J5.pin1, DHT2.DATA
  N11: J5.pin2, DHT2.VDD
  N12: J5.pin3, DHT2.GND
  N13: LED3.anode, R3.Pin_1
  N14: LED4.anode, R4.Pin_1

custom parts:
  NodeMCU V1.0: ESP8266 based NodeMCU
  DHT11 Humitidy and Temperature Sensor: DHT11 Humidity and Temperature Sensor
